# Fritzing sketch grunting_circuit (saved by Fritzing 0.9.2b)
breadboards: 1

parts:
  ADXL1 = ADXL335 Accelerometer Breakout
  パーツ1 = Arduino Pro Mini v13
  パーツ2 = Audio FX Sound Board + 2x2W Amp
  LED1 = LED - 5mm [color="Red (633nm)" package="5 mm [THT]"]
  S2 = Round Pushbutton
  R1 = Resistor [tolerance=±5% resistance=1.5k package=THT]
  SP1 = SPEAKER [package=pcb_mount_speaker]

nets:
  GND: ADXL1.GND, パーツ1.GND, パーツ2.UG, パーツ2.GND, LED1.cathode, R1.Pin_0
  N1: ADXL1.Xout, パーツ1.A0
  N2: ADXL1.Yout, パーツ1.A1
  N3: ADXL1.Zout, パーツ1.A2
  N4: パーツ1.D9_PWM, LED1.anode
  N5: パーツ1.D6_PWM, パーツ2.RX
  N6: パーツ1.D5_PWM, パーツ2.TX
  N7: パーツ1.D4, パーツ2.RST
  N8: パーツ1.D2, S2.leg0, R1.Pin_1
  N9: パーツ2.VIN, S2.leg1
  N10: パーツ2.L-, SP1.+
  N11: パーツ2.L+, SP1.-

custom parts:
  ADXL335 Accelerometer Breakout: ADXL335 Accelerometer Breakout board
  Audio FX Sound Board + 2x2W Amp: The Adafruit Sound Board, the fastest way to add audio effects to a project!
