# Fritzing sketch grunting_circuit2 (saved by Fritzing 0.9.2b)
breadboards: 1

parts:
  ADXL1 = ADXL335 Accelerometer Breakout
  パーツ1 = Arduino Pro Mini v13
  パーツ2 = Audio FX Sound Board + 2x2W Amp
  S2 = Round Pushbutton
  R1 = Resistor [tolerance=±5% resistance=1.5k package=THT]
  LED1 = LED - 5mm [color="Red (633nm)" package="5 mm [THT]"]
  U1 = LIPO-110mAh [package=lipo-110]
  S3 = Momentary Switch [package=ksa_sealed_tac_switch]

nets:
  VIN: ADXL1.Vin, パーツ1.RAW, パーツ2.VIN, S2.leg0, U1.+, S3.4
  GND: ADXL1.GND, パーツ1.GND, パーツ2.UG, パーツ2.5, R1.Pin_1, LED1.cathode, U1.-
  N1: ADXL1.Xout, パーツ1.A0
  N2: ADXL1.Yout, パーツ1.A1
  N3: ADXL1.Zout, パーツ1.A2
  N4: パーツ1.D9_PWM, LED1.anode
  N5: パーツ1.D6_PWM, パーツ2.RX
  N6: パーツ1.D5_PWM, パーツ2.TX
  N7: パーツ1.D4, パーツ2.RST, S3.3
  N8: パーツ1.D2, S2.leg1, R1.Pin_0

custom parts:
  ADXL335 Accelerometer Breakout: ADXL335 Accelerometer Breakout board
  Audio FX Sound Board + 2x2W Amp: The Adafruit Sound Board, the fastest way to add audio effects to a project!
